# Fritzing sketch ioTank (saved by Fritzing 0.9.2b)
circuit board: 1.11cm x 1.27cm
circuit board: 1.27cm x 1.11cm
circuit board: 3.40093cm x 7.43001cm
breadboards: 1

parts:
  DHT11 = DHT11 Humitidy and Temperature Sensor
  10k = Resistor [tolerance=±1% resistance=10k package=THT]
  T1 = Temperature Sensor (Thermistor) [thermistor_type=NTC package=THT]
  MCP3008 = IC, DIP package, 16 pins [chip_label=MPC3008]
  ioTank = NodeMCU V1.0
  10k_2 = Resistor [tolerance=±1% resistance=10k package=THT]

nets:
  VDD: DHT11.VDD, 10k.Pin_1, MCP3008.pin15, MCP3008.pin16, ioTank.3V3, 10k_2.Pin_0
  N1: DHT11.DATA, ioTank.D4, 10k_2.Pin_1
  GND: DHT11.GND, T1.pin_0, MCP3008.pin14, ioTank.GND
  N2: 10k.Pin_0, T1.pin_1, MCP3008.pin1
  N3: MCP3008.pin10, ioTank.D8
  N4: MCP3008.pin11, ioTank.D7
  N5: MCP3008.pin12, ioTank.D6
  N6: MCP3008.pin13, ioTank.D5

notes:
  Object Syndicate
  Herpien.com
  UVI
  Lux
  Designed in Colorado    USA
  +

custom parts:
  DHT11 Humitidy and Temperature Sensor: DHT11 Humidity and Temperature Sensor
  NodeMCU V1.0: ESP8266 based NodeMCU
